# Fritzing sketch base_radio (saved by Fritzing 0.9.3b)
breadboards: 1

parts:
  M2 = NRF24L01-BO [package=THT]
  Componente4 = Arduino Nano Every
  Componente5 = Arduino MKR WIFI 1010
  Componente6 = Bi-Directional Logic Level Converter [part_number=BOB-12009]  # not connected
  LED1 = LED - 3mm [color="Green (570nm)" package="3 mm [THT]"]
  LED2 = LED - 3mm [color="Yellow (595nm)" package="3 mm [THT]"]

nets:
  N1: M2.IRQ, M2.M1, Componente4.D12~/MISO
  VCC: M2.M0, M2.VCC, Componente4.D11/MOSI, Componente4.+5V
  GND: M2.SCK, M2.GND, Componente4.GND, Componente4.D13~
  N2: M2.CSN, Componente4.D8
  N3: M2.CE, Componente4.D7
  N4: Componente4.RESET, Componente4.A7
  N5: Componente5.A4, Componente5.D14_<--_TX
  N6: Componente5.GND, LED1.cathode, LED2.cathode
  N7: Componente5.D3_PWM, LED2.anode
  N8: Componente5.D5_PWM, LED1.anode

custom parts:
  NRF24L01-BO: NRF24L01-BO breakout board for the NRF24L01. Pcb view suppressed as unneeded.
  Arduino Nano Every: The Nano Every is Arduino’s 5V compatible board in the smallest available form factor: 45x18mm! The Arduino Nano is the preferred board for many projects requiring a small and easy to use microcontroller board. The small footprint and low price, make the Nano Every particularly suited for wearable inventions, low cost robotics, electronic musical instruments, and general use to control smaller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
  Arduino MKR WIFI 1010: The MKR WIFI 1010 is a significant improvement on the MKR 1000 WIFI. It's equipped with an ESP32 module made by U-BLOX. This board aims to speed up and simplify the prototyping of WiFi based IoT applications thanks to the flexibility of the ESP32 module and its low power consumption. The board is composed of three main blocks: SAMD21 Cortex-M0+ 32bit Low Power ARM MCU; U-BLOX NINA-W10 Series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
  Bi-Directional Logic Level Converter: Description: If you've ever tried to connect a 3.3V device to a 5V system, you know what a challenge it can be. The SparkFun bi-directional logic level converter is a small device that safely steps down 5V signals to 3.3V AND steps up 3.3V to 5V at the same time. This level converter also works with 2.8V and 1.8V devices. What really separates this Logic level converter from our previous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
