# Fritzing sketch fly_radio (saved by Fritzing 0.9.3b)
breadboards: 1

parts:
  M1 = NRF24L01-BO [package=THT]
  Componente3 = Arduino Nano Every
  Componente4 = Adafruit BMP180
  Mod1 = KY-015 Temperature & Humidity Sensor Module [package="Breakout board"]
  Componente5 = MQ-7 breakout
  LED1 = LED - 3mm [color="Yellow (595nm)" package="3 mm [THT]"]
  LED2 = LED - 3mm [color="Green (570nm)" package="3 mm [THT]"]

nets:
  N1: M1.IRQ, M1.M1, Componente3.D12~/MISO
  VCC: M1.M0, M1.VCC, Componente3.D11/MOSI, Componente3.+5V, Componente4.+5V, Mod1.Vin, Componente5.VCC
  GND: M1.SCK, M1.GND, Componente3.GND, Componente3.D13~, Componente4.GND, Mod1.-, Componente5.GND, LED1.cathode, LED2.cathode
  N2: M1.CSN, Componente3.D8
  N3: M1.CE, Componente3.D7
  N4: Componente3.RESET, Componente3.A7
  N5: Componente3.D2, Mod1.S
  N6: Componente3.D3~, LED1.anode
  N7: Componente3.D4, LED2.anode
  N8: Componente3.A5, Componente4.SCL
  N9: Componente3.A4, Componente4.SDA
  N10: Componente3.A1, Componente5.AO

custom parts:
  NRF24L01-BO: NRF24L01-BO breakout board for the NRF24L01. Pcb view suppressed as unneeded.
  Arduino Nano Every: The Nano Every is Arduino’s 5V compatible board in the smallest available form factor: 45x18mm! The Arduino Nano is the preferred board for many projects requiring a small and easy to use microcontroller board. The small footprint and low price, make the Nano Every particularly suited for wearable inventions, low cost robotics, electronic musical instruments, and general use to control smaller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
  Adafruit BMP180: This precision sensor from Bosch is the best low-cost sensing solution for measuring barometric pressure and temperature. Because pressure changes with altitude you can also use it as an altimeter! The sensor is soldered onto a PCB with a 3.3V regulator, I2C level shifter and pull-up resistors on the I2C pins. The BMP180 is the next-generation of sensors from Bosch, and replaces the BMP085.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
  KY-015 Temperature & Humidity Sensor Module: KY-015 temperature and humidity sensor module, provides a low-latency serial interface to measure humidity and temperature.
  MQ-7 breakout: SKU: 101282
