# Fritzing sketch board1 (saved by Fritzing 0.9.3b)
breadboards: 1

parts:
  Componente4 = Arduino Mega 2560 (Rev3)
  Componente6 = Bi-Directional Logic Level Converter
  Mod1 = Arduino MKR Wifi 1010
  Mod2 = MQ-7 breakout
  Componente8 = MQ-7 breakout
  Mod3 = KY-015 Temperature & Humidity Sensor Module [package="Breakout board"]
  BMP1 = BMP180

nets:
  N1: Componente4.A0, Componente8.AO
  N2: Componente4.A1, Mod2.DO
  N3: Componente4.D21/SCL, Componente6.HV1, BMP1.SCL
  N4: Componente4.D20/SDA, Componente6.HV2, BMP1.SDA
  VCC: Componente4.3V3, Componente6.LV, Componente6.HV, Mod2.VCC, Componente8.VCC, Mod3.Vin, BMP1.VIN
  N5: Componente4.D22, Mod3.S
  N6: Componente4.D23, Mod2.AO
  N7: Componente6.LV1, Mod1.D12/SCL
  N8: Componente6.LV2, Mod1.D11/SDA
  N9: Componente6.GND#3, Mod1.GND
  GND: Componente6.GND#8, Mod2.GND, Componente8.GND, Mod3.-, BMP1.GND

custom parts:
  Bi-Directional Logic Level Converter: Description: If you've ever tried to connect a 3.3V device to a 5V system, you know what a challenge it can be. The SparkFun bi-directional logic level converter is a small device that safely steps down 5V signals to 3.3V AND steps up 3.3V to 5V at the same time. This level converter also works with 2.8V and 1.8V devices. What really separates this Logic level converter from our previous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
  Arduino MKR Wifi 1010: Arduino MKR Wifi 1010, SAMD21 Cortex-M0+ 32bit Low Power ARM MCU,Flash Memory 256 KB, SRAM 32KB, 48mhz clock, Ublok Wifi interface.
  MQ-7 breakout: MQ-5 gas sensor
  MQ-7 breakout: SKU: 101282
  KY-015 Temperature & Humidity Sensor Module: KY-015 temperature and humidity sensor module, provides a low-latency serial interface to measure humidity and temperature.
