# Fritzing sketch board2 (saved by Fritzing 0.9.3b)
breadboards: 2

parts:
  Componente1 = Arduino Nano Every
  Componente2 = Arduino MKR WIFI 1010
  LLC1 = Logic Level Converter [package="Breakout board"]
  YwRobot_Power_Supply1 = YwRobot Breadboard Power Supply [part_number=545043]
  Componente3 = MQ-7 breakout  # not connected
  Componente4 = Adafruit BMP180
  Mod1 = KY-015 Temperature & Humidity Sensor Module [package="Breakout board"]  # not connected
  LED1 = LED - 3mm [color="Yellow (592nm)" package="3 mm [THT]"]
  LED3 = LED - 3mm [color="Green (570nm)" package="3 mm [THT]"]
  R1 = Resistor [tolerance=±5% resistance=220 package=THT]
  R2 = Resistor [tolerance=±5% resistance=220 package=THT]
  LED4 = LED - 3mm [color="Yellow (592nm)" package="3 mm [THT]"]
  LED5 = LED - 3mm [color="Green (570nm)" package="3 mm [THT]"]

nets:
  N1: Componente1.RESET, Componente1.A7
  N2: Componente1.GND, Componente1.D13~
  N3: Componente1.D11/MOSI, Componente1.+5V
  N4: Componente2.A4, Componente2.D14_<--_TX
  N5: Componente2.D11/SDA, LLC1.LV4, Componente4.SDA
  N6: Componente2.D12/SCL, LLC1.LV1, Componente4.SCL
  N7: Componente2.D4_PWM, LED4.anode
  N8: Componente2.D5_PWM, LED5.anode
  +5V: LLC1.LV, YwRobot_Power_Supply1.VCC#5, YwRobot_Power_Supply1.VCC#6, Componente4.+5V, Componente4.+3V3
  N9: LLC1.L-GND, YwRobot_Power_Supply1.GND#11, YwRobot_Power_Supply1.GND#12, Componente4.GND, R2.Pin_1
  N10: YwRobot_Power_Supply1.VCC#9, YwRobot_Power_Supply1.VCC#10
  N11: YwRobot_Power_Supply1.GND#13, YwRobot_Power_Supply1.GND#14
  N12: LED1.cathode, LED3.cathode, R1.Pin_0
  N13: R2.Pin_0, LED4.cathode, LED5.cathode

custom parts:
  Arduino Nano Every: The Nano Every is Arduino’s 5V compatible board in the smallest available form factor: 45x18mm! The Arduino Nano is the preferred board for many projects requiring a small and easy to use microcontroller board. The small footprint and low price, make the Nano Every particularly suited for wearable inventions, low cost robotics, electronic musical instruments, and general use to control smaller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
  Arduino MKR WIFI 1010: The MKR WIFI 1010 is a significant improvement on the MKR 1000 WIFI. It's equipped with an ESP32 module made by U-BLOX. This board aims to speed up and simplify the prototyping of WiFi based IoT applications thanks to the flexibility of the ESP32 module and its low power consumption. The board is composed of three main blocks: SAMD21 Cortex-M0+ 32bit Low Power ARM MCU; U-BLOX NINA-W10 Series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
  Logic Level Converter: 5V to/from 3.3V logic level converter
  YwRobot Breadboard Power Supply: The YwRobot Breadboard Power Supply (MB-V2) has two power rails; they can be 5V or 3V3. Power to the module can be provided through the female USB socket or through the A10 (female) 2.1mm power jack.
  MQ-7 breakout: SKU: 101282
  Adafruit BMP180: This precision sensor from Bosch is the best low-cost sensing solution for measuring barometric pressure and temperature. Because pressure changes with altitude you can also use it as an altimeter! The sensor is soldered onto a PCB with a 3.3V regulator, I2C level shifter and pull-up resistors on the I2C pins. The BMP180 is the next-generation of sensors from Bosch, and replaces the BMP085.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
  KY-015 Temperature & Humidity Sensor Module: KY-015 temperature and humidity sensor module, provides a low-latency serial interface to measure humidity and temperature.
