# Fritzing sketch pcb1_front_fly_radio (saved by Fritzing 0.9.3b)
breadboards: 1
perfboards: 1

parts:
  J2 = single row smd female pin header, 15 pins [form="♀ (female)"]
  M1 = NRF24L01-BO [package=THT]  # not connected
  J1 = single row smd female pin header, 15 pins [form="♀ (female)"]
  J5 = male pin header, 3 pins [form="♂ (male)"]  # not connected
  J6 = male pin header, 4 pins [form="♂ (male)"]  # not connected
  J7 = male pin header, 3 pins [form="♂ (male)"]  # not connected
  J8 = male pin header, 6 pins [form="♂ (male)"]  # not connected
  J9 = male pin header, 4 pins [form="♂ (male)"]  # not connected
  Componente2 = MQ-7 breakout  # not connected
  J3 = male pin header, 2 pins [form="♂ (male)"]  # not connected
  Componente1 = Arduino Nano Every
  J4 = male pin header, 6 pins [form="♂ (male)"]  # not connected

nets:
  N1: J2.pin1, Componente1.D12~/MISO
  N2: J2.pin2, J1.pin12, Componente1.D11/MOSI, Componente1.+5V
  N3: J2.pin3, Componente1.D10~
  N4: J2.pin4, Componente1.D9~
  N5: J2.pin5, Componente1.D8
  N6: J2.pin6, Componente1.D7
  N7: J2.pin7, Componente1.D6~
  N8: J2.pin8, Componente1.D5~
  N9: J2.pin9, Componente1.D4
  N10: J2.pin10, Componente1.D3~
  N11: J2.pin11, Componente1.D2
  N12: J2.pin12, J1.pin1, J1.pin14, Componente1.GND, Componente1.D13~
  N13: J2.pin13, J1.pin11, Componente1.RESET, Componente1.A7
  N14: J2.pin14, Componente1.RX
  N15: J2.pin15, Componente1.TX
  N16: J1.pin2, Componente1.3V3
  N17: J1.pin3, Componente1.AREF
  N18: J1.pin4, Componente1.A0
  N19: J1.pin5, Componente1.A1
  N20: J1.pin6, Componente1.A2
  N21: J1.pin7, Componente1.A3
  N22: J1.pin8, Componente1.A4
  N23: J1.pin9, Componente1.A5
  N24: J1.pin10, Componente1.A6
  N25: J1.pin15, Componente1.VIN

custom parts:
  NRF24L01-BO: NRF24L01-BO breakout board for the NRF24L01. Pcb view suppressed as unneeded.
  MQ-7 breakout: SKU: 101282
  Arduino Nano Every: The Nano Every is Arduino’s 5V compatible board in the smallest available form factor: 45x18mm! The Arduino Nano is the preferred board for many projects requiring a small and easy to use microcontroller board. The small footprint and low price, make the Nano Every particularly suited for wearable inventions, low cost robotics, electronic musical instruments, and general use to control smaller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
